# Fritzing sketch zu (saved by Fritzing 0.9.4)

parts:
  M5Stack_Core_(Back)1 = M5Stack Core (Back)
  HC-SR04_Sensor_1 = HC-SR04 Ultrasonic Distance Sensor

nets:
  GND: M5Stack_Core_(Back)1.Gnd, HC-SR04_Sensor_1.GND
  5V: M5Stack_Core_(Back)1.5V, HC-SR04_Sensor_1.VCC
  N1: M5Stack_Core_(Back)1.5, HC-SR04_Sensor_1.ECHO
  N2: M5Stack_Core_(Back)1.2, HC-SR04_Sensor_1.TRIG

custom parts:
  M5Stack Core (Back): M5Stack ESP32 development kit
